// Digital circuit mips_PC+4.dig as structural Verilog
module mips_PC_4 (
  input  Clock
);

  wire [31:0] PC_p1, PC_p3;

  // mips_reg32bits PC: pin names not known; wires that end beside it: PC_p1, Clock, PC_p3
  mips_somador32bits Soma32bits (.A(PC_p3), .B(32'h4), .Cin(1'b0), .\Saída (PC_p1));  // open: Cout
endmodule
