// Digital circuit mips_aux.dig as structural Verilog
module mips_aux (
  input  Clock
);

  wire mips_controle_1_p2, mips_extensor16_32_1_p2, mips_memoria_dado_1_p3, mips_ula32bits_newmodel_1_p7;
  wire [1:0] mips_controle_1_p3;
  wire [31:0] \mips_bancodereg_1_lê_dado_1 , \mips_bancodereg_1_lê_dado_2 , \mips_memoria_instrução_1_d ,
       PC_p1, PC_p3;

  // mips_reg32bits PC: pin names not known; wires that end beside it: PC_p1, Clock, PC_p3
  mips_somador32bits Soma32bits (.A(PC_p3), .B(32'h4), .Cin(1'b0), .\Saída (PC_p1));  // open: Cout
  \mips_memoria_instrução  \mips_memoria_instrução_1  (.A(PC_p3), .D(\mips_memoria_instrução_1_d ));
  // mips_deslocamento26_28 mips_deslocamento26_28_1: pin names not known; wires that end beside it: \mips_memoria_instrução_1_d [25:0]
  // mips_controle mips_controle_1: pin names not known; wires that end beside it: \mips_memoria_instrução_1_d [31:26], mips_controle_1_p2, mips_controle_1_p3[0], mips_controle_1_p3[1]
  mips_bancodeReg mips_bancodereg_1 (
    .Escrever(mips_controle_1_p2), .\Lê_Reg__de_Leitura_1 (\mips_memoria_instrução_1_d [25:21]),
    .\Lê_Reg__de_Leitura_2 (\mips_memoria_instrução_1_d [20:16]),
    .\Lê_Dado_1 (\mips_bancodereg_1_lê_dado_1 ), .\Lê_Dado_2 (\mips_bancodereg_1_lê_dado_2 ));  // open: Escreve_Dado, Escreve_Reg
  // mips_extensor16_32 mips_extensor16_32_1: pin names not known; wires that end beside it: \mips_memoria_instrução_1_d [15:0], mips_extensor16_32_1_p2
  // mips_ULA32bits_newmodel mips_ula32bits_newmodel_1: pin names not known; wires that end beside it: 1'b0, 1'b0, 1'b0, mips_controle_1_p3, \mips_bancodereg_1_lê_dado_1 , mips_extensor16_32_1_p2, mips_ula32bits_newmodel_1_p7
  // mips_memoria_dado mips_memoria_dado_1: pin names not known; wires that end beside it: mips_ula32bits_newmodel_1_p7, \mips_bancodereg_1_lê_dado_2 , mips_memoria_dado_1_p3, mips_memoria_dado_1_p3
endmodule
