// Digital circuit mips_auxiliar_lixo.dig as structural Verilog
module mips_auxiliar_lixo (
  input  [15:0] A,
  input  Id,
  output [15:0] D
);

  wire and_1_out;

  and and_1 (and_1_out, ~A[15], Id);  // And
  ROM #(.AddrBits(15), .isProgramMemory("true"), .Bits(16), .Addr_Bits(15)) rom_1 (.A(A[14:0]), .sel(and_1_out), .D(D));
  RAMDualPort ramdualport_1 ();  // open: A, Din, str, C, ld, D
  BlockRAMDualPort blockramdualport_1 ();  // open: A, Din, str, C, D

  // Notes on the sheet:
  //   D: bidirectional data bus
  //   {{de Der bidirektionelle Datenbus}}
  //   A: address bus
  //   {{de Der Adressbus}}
  //   contents of rom_1 (hex, n*v repeats v):
  //   1e,14,2020,1,c,c0,2400,0,4,c,0,8,656c,2057,6c64
endmodule
