// Digital circuit mips_decodificador.dig as structural Verilog
module mips_decodificador (
  input  [4:0] Entrada,
  output Saida0,
  output Saida1,
  output Saida2,
  output Saida3,
  output Saida4,
  output Saida5,
  output Saida6,
  output Saida7,
  output Saida8,
  output Saida9,
  output Saida10,
  output Saida11,
  output Saida12,
  output Saida13,
  output Saida14,
  output Saida15,
  output Saida16,
  output Saida17,
  output Saida18,
  output Saida19,
  output Saida20,
  output Saida21,
  output Saida22,
  output Saida23,
  output Saida24,
  output Saida25,
  output Saida26,
  output Saida27,
  output Saida28,
  output Saida29,
  output Saida30,
  output Saida31
);

  and and_1 (Saida0, ~Entrada[4], ~Entrada[3], ~Entrada[2], ~Entrada[1], ~Entrada[0]);  // And
  and and_2 (Saida1, ~Entrada[4], ~Entrada[3], ~Entrada[2], ~Entrada[1], Entrada[0]);  // And
  and and_3 (Saida2, ~Entrada[4], ~Entrada[3], ~Entrada[2], Entrada[1], ~Entrada[0]);  // And
  and and_4 (Saida3, ~Entrada[4], ~Entrada[3], ~Entrada[2], Entrada[1], Entrada[0]);  // And
  and and_5 (Saida4, ~Entrada[4], ~Entrada[3], Entrada[2], ~Entrada[1], ~Entrada[0]);  // And
  and and_6 (Saida5, ~Entrada[4], ~Entrada[3], Entrada[2], ~Entrada[1], Entrada[0]);  // And
  and and_7 (Saida6, ~Entrada[4], ~Entrada[3], Entrada[2], Entrada[1], ~Entrada[0]);  // And
  and and_8 (Saida7, ~Entrada[4], ~Entrada[3], Entrada[2], Entrada[1], Entrada[0]);  // And
  and and_9 (Saida8, ~Entrada[4], Entrada[3], ~Entrada[2], ~Entrada[1], ~Entrada[0]);  // And
  and and_10 (Saida9, ~Entrada[4], Entrada[3], ~Entrada[2], ~Entrada[1], Entrada[0]);  // And
  and and_11 (Saida10, ~Entrada[4], Entrada[3], ~Entrada[2], Entrada[1], ~Entrada[0]);  // And
  and and_12 (Saida11, ~Entrada[4], Entrada[3], ~Entrada[2], Entrada[1], Entrada[0]);  // And
  and and_13 (Saida12, ~Entrada[4], Entrada[3], Entrada[2], ~Entrada[1], ~Entrada[0]);  // And
  and and_14 (Saida13, ~Entrada[4], Entrada[3], Entrada[2], ~Entrada[1], Entrada[0]);  // And
  and and_15 (Saida14, ~Entrada[4], Entrada[3], Entrada[2], Entrada[1], ~Entrada[0]);  // And
  and and_16 (Saida15, ~Entrada[4], Entrada[3], Entrada[2], Entrada[1], Entrada[0]);  // And
  and and_17 (Saida16, Entrada[4], ~Entrada[3], ~Entrada[2], ~Entrada[1], ~Entrada[0]);  // And
  and and_18 (Saida17, Entrada[4], ~Entrada[3], ~Entrada[2], ~Entrada[1], Entrada[0]);  // And
  and and_19 (Saida18, Entrada[4], ~Entrada[3], ~Entrada[2], Entrada[1], ~Entrada[0]);  // And
  and and_20 (Saida19, Entrada[4], ~Entrada[3], ~Entrada[2], Entrada[1], Entrada[0]);  // And
  and and_21 (Saida20, Entrada[4], ~Entrada[3], Entrada[2], ~Entrada[1], ~Entrada[0]);  // And
  and and_22 (Saida21, Entrada[4], ~Entrada[3], Entrada[2], ~Entrada[1], Entrada[0]);  // And
  and and_23 (Saida22, Entrada[4], ~Entrada[3], Entrada[2], Entrada[1], ~Entrada[0]);  // And
  and and_24 (Saida23, Entrada[4], ~Entrada[3], Entrada[2], Entrada[1], Entrada[0]);  // And
  and and_25 (Saida24, Entrada[4], Entrada[3], ~Entrada[2], ~Entrada[1], ~Entrada[0]);  // And
  and and_26 (Saida25, Entrada[4], Entrada[3], ~Entrada[2], ~Entrada[1], Entrada[0]);  // And
  and and_27 (Saida26, Entrada[4], Entrada[3], ~Entrada[2], Entrada[1], ~Entrada[0]);  // And
  and and_28 (Saida27, Entrada[4], Entrada[3], ~Entrada[2], Entrada[1], Entrada[0]);  // And
  and and_29 (Saida28, Entrada[4], Entrada[3], Entrada[2], ~Entrada[1], ~Entrada[0]);  // And
  and and_30 (Saida29, Entrada[4], Entrada[3], Entrada[2], ~Entrada[1], Entrada[0]);  // And
  and and_31 (Saida30, Entrada[4], Entrada[3], Entrada[2], Entrada[1], ~Entrada[0]);  // And
  and and_32 (Saida31, Entrada[4], Entrada[3], Entrada[2], Entrada[1], Entrada[0]);
endmodule
