// Digital circuit mips_memoria_dado.dig as structural Verilog
module mips_memoria_dado (
  input  [31:0] A,
  input  [31:0] Din,
  input  [31:0] LerMem,
  input  [31:0] EscrevMem,
  input  Clock,
  output [31:0] D
);

  wire not_1_out;

  not not_1 (not_1_out, Clock);
  RAMDualPort #(.AddrBits(24), .Bits(32)) ramdualport_1 (
    .A(A[23:0]), .Din(Din), .str(EscrevMem[0]), .C(not_1_out), .ld(LerMem[0]), .D(D));
  // Pins of 24 and 32 bits meet at A
  // Pins of 1 and 32 bits meet at EscrevMem
  // Pins of 1 and 32 bits meet at LerMem

  // Notes on the sheet:
  //   D: bidirectional data bus
  //   {{de Der bidirektionelle Datenbus}}
  //   A: address bus
  //   {{de Der Adressbus}}
  //   Din: Dados pra armazenar
  //   LerMem: address bus
  //   {{de Der Adressbus}}
  //   EscrevMem: address bus
  //   {{de Der Adressbus}}
endmodule
