// Digital circuit mips_mux2_32bits.dig as structural Verilog
module mips_mux2_32bits (
  input  [31:0] Entrada0,
  input  [31:0] Entrada1,
  input  \Seleção ,
  output [31:0] Saida
);

  wire [31:0] and_1_out, and_2_out;

  assign and_1_out = Entrada0 & ~{{31{1'b0}}, \Seleção };  // And and_1, 32 bits wide
  assign and_2_out = {{31{1'b0}}, \Seleção } & Entrada1;  // And and_2, 32 bits wide
  assign Saida = and_1_out | and_2_out;  // Or or_1, 32 bits wide
endmodule
