// Digital circuit mips_somador32bits.dig as structural Verilog
module mips_somador32bits (
  input  [31:0] A,
  input  [31:0] B,
  input  Cin,
  output Cout,
  output [31:0] \Saída 
);

  wire undriven, undriven_2, undriven_3, undriven_4, undriven_5, undriven_6, undriven_7, undriven_8,
       undriven_9, undriven_10, undriven_11, undriven_12, undriven_13, undriven_14, undriven_15, undriven_16,
       undriven_17, undriven_18, undriven_19, undriven_20, undriven_21, undriven_22, undriven_23,
       undriven_24, undriven_25, undriven_26, undriven_27, undriven_28, undriven_29, undriven_30, undriven_31;

  mips_somacomplet mips_somacomplet_1 (.Entrada0(A[0]), .Entrada1(B[0]), .VemUm(Cin));  // open: Saida, VaiUm
  mips_somacomplet mips_somacomplet_2 (.Entrada0(A[1]), .Entrada1(B[1]), .VemUm(undriven_31));  // open: Saida, VaiUm
  mips_somacomplet mips_somacomplet_3 (.Entrada0(A[2]), .Entrada1(B[2]), .VemUm(undriven_30));  // open: Saida, VaiUm
  mips_somacomplet mips_somacomplet_4 (.Entrada0(A[3]), .Entrada1(B[3]), .VemUm(undriven_29));  // open: Saida, VaiUm
  mips_somacomplet mips_somacomplet_5 (.Entrada0(A[4]), .Entrada1(B[4]), .VemUm(undriven_28));  // open: Saida, VaiUm
  mips_somacomplet mips_somacomplet_6 (.Entrada0(A[5]), .Entrada1(B[5]), .VemUm(undriven_27));  // open: Saida, VaiUm
  mips_somacomplet mips_somacomplet_7 (.Entrada0(A[6]), .Entrada1(B[6]), .VemUm(undriven_26));  // open: Saida, VaiUm
  mips_somacomplet mips_somacomplet_8 (.Entrada0(A[7]), .Entrada1(B[7]), .VemUm(undriven_25));  // open: Saida, VaiUm
  mips_somacomplet mips_somacomplet_9 (.Entrada0(A[8]), .Entrada1(B[8]), .VemUm(undriven_24));  // open: Saida, VaiUm
  mips_somacomplet mips_somacomplet_10 (.Entrada0(A[9]), .Entrada1(B[9]), .VemUm(undriven_23));  // open: Saida, VaiUm
  mips_somacomplet mips_somacomplet_11 (.Entrada0(A[10]), .Entrada1(B[10]), .VemUm(undriven_22));  // open: Saida, VaiUm
  mips_somacomplet mips_somacomplet_12 (.Entrada0(A[11]), .Entrada1(B[11]), .VemUm(undriven_21));  // open: Saida, VaiUm
  mips_somacomplet mips_somacomplet_13 (.Entrada0(A[12]), .Entrada1(B[12]), .VemUm(undriven_20));  // open: Saida, VaiUm
  mips_somacomplet mips_somacomplet_14 (.Entrada0(A[13]), .Entrada1(B[13]), .VemUm(undriven_19));  // open: Saida, VaiUm
  mips_somacomplet mips_somacomplet_15 (.Entrada0(A[14]), .Entrada1(B[14]), .VemUm(undriven_18));  // open: Saida, VaiUm
  mips_somacomplet mips_somacomplet_16 (.Entrada0(A[15]), .Entrada1(B[15]), .VemUm(undriven_17));  // open: Saida, VaiUm
  mips_somacomplet mips_somacomplet_17 (.Entrada0(A[16]), .Entrada1(B[16]), .VemUm(undriven));  // open: Saida, VaiUm
  mips_somacomplet mips_somacomplet_18 (.Entrada0(A[17]), .Entrada1(B[17]), .VemUm(undriven_2));  // open: Saida, VaiUm
  mips_somacomplet mips_somacomplet_19 (.Entrada0(A[18]), .Entrada1(B[18]), .VemUm(undriven_3));  // open: Saida, VaiUm
  mips_somacomplet mips_somacomplet_20 (.Entrada0(A[19]), .Entrada1(B[19]), .VemUm(undriven_4));  // open: Saida, VaiUm
  mips_somacomplet mips_somacomplet_21 (.Entrada0(A[20]), .Entrada1(B[20]), .VemUm(undriven_5));  // open: Saida, VaiUm
  mips_somacomplet mips_somacomplet_22 (.Entrada0(A[21]), .Entrada1(B[21]), .VemUm(undriven_6));  // open: Saida, VaiUm
  mips_somacomplet mips_somacomplet_23 (.Entrada0(A[22]), .Entrada1(B[22]), .VemUm(undriven_7));  // open: Saida, VaiUm
  mips_somacomplet mips_somacomplet_24 (.Entrada0(A[23]), .Entrada1(B[23]), .VemUm(undriven_8));  // open: Saida, VaiUm
  mips_somacomplet mips_somacomplet_25 (.Entrada0(A[24]), .Entrada1(B[24]), .VemUm(undriven_9));  // open: Saida, VaiUm
  mips_somacomplet mips_somacomplet_26 (.Entrada0(A[25]), .Entrada1(B[25]), .VemUm(undriven_10));  // open: Saida, VaiUm
  mips_somacomplet mips_somacomplet_27 (.Entrada0(A[26]), .Entrada1(B[26]), .VemUm(undriven_11));  // open: Saida, VaiUm
  mips_somacomplet mips_somacomplet_28 (.Entrada0(A[27]), .Entrada1(B[27]), .VemUm(undriven_12));  // open: Saida, VaiUm
  mips_somacomplet mips_somacomplet_29 (.Entrada0(A[28]), .Entrada1(B[28]), .VemUm(undriven_13));  // open: Saida, VaiUm
  mips_somacomplet mips_somacomplet_30 (.Entrada0(A[29]), .Entrada1(B[29]), .VemUm(undriven_14));  // open: Saida, VaiUm
  mips_somacomplet mips_somacomplet_31 (.Entrada0(A[30]), .Entrada1(B[30]), .VemUm(undriven_15));  // open: Saida, VaiUm
  mips_somacomplet mips_somacomplet_32 (.Entrada0(A[31]), .Entrada1(B[31]), .VemUm(undriven_16));  // open: Saida, VaiUm
endmodule
