// Digital circuit mips_testando_instrucao_ADDI.dig as structural Verilog
module mips_testando_instrucao_ADDI (
  input  [31:0] in_3,
  input  [31:0] in_4,
  input  in_5,
  output [31:0] Saida0,
  output [31:0] Saida1
);

  wire [4:0] \mips_memoria_instrução_1_d_2 , \mips_memoria_instrução_1_d_3 ;
  wire [31:0] \mips_memoria_instrução_1_d ;

  \mips_memoria_instrução  \mips_memoria_instrução_1  (
    .A(in_3),
    .D({\mips_memoria_instrução_1_d [31:26], \mips_memoria_instrução_1_d_3 , \mips_memoria_instrução_1_d_2 , \mips_memoria_instrução_1_d [15:0]}));
  mips_bancodeReg mips_bancodereg_1 (
    .Escrever(in_5), .Escreve_Dado(in_4), .Escreve_Reg(\mips_memoria_instrução_1_d_2 ),
    .\Lê_Reg__de_Leitura_1 (\mips_memoria_instrução_1_d_3 ),
    .\Lê_Reg__de_Leitura_2 (\mips_memoria_instrução_1_d_2 ), .\Lê_Dado_1 (Saida0), .\Lê_Dado_2 (Saida1));
endmodule
