// Digital circuit mips_PC+4.dig as structural Verilog
module mips_PC_4 (
  input  Clock,
  input  Clear,
  output [31:0] Saida
);

  wire [31:0] \Soma32bits_saída ;

  mips_PC mips_pc_1 (.Entrada(\Soma32bits_saída ), .Clock(Clock), .Clear(Clear), .Saida(Saida));
  mips_somador32bits Soma32bits (.A(Saida), .B(32'h4), .Cin(1'b0), .\Saída (\Soma32bits_saída ));  // open: Cout
endmodule
