// Digital circuit mips_PC.dig as structural Verilog
module mips_PC (
  input  [31:0] Entrada,
  input  Clock,
  input  Clear,
  output [31:0] Saida
);

  mips_flipflopD_clear mips_flipflopd_clear_1 (.Clock(Clock), .D(Entrada[0]), .Clear(Clear), .Q(Saida[0]));  // open: nQ
  mips_flipflopD_clear mips_flipflopd_clear_2 (.Clock(Clock), .D(Entrada[1]), .Clear(Clear), .Q(Saida[1]));  // open: nQ
  mips_flipflopD_clear mips_flipflopd_clear_3 (.Clock(Clock), .D(Entrada[2]), .Clear(Clear), .Q(Saida[2]));  // open: nQ
  mips_flipflopD_clear mips_flipflopd_clear_4 (.Clock(Clock), .D(Entrada[3]), .Clear(Clear), .Q(Saida[3]));  // open: nQ
  mips_flipflopD_clear mips_flipflopd_clear_5 (.Clock(Clock), .D(Entrada[4]), .Clear(Clear), .Q(Saida[4]));  // open: nQ
  mips_flipflopD_clear mips_flipflopd_clear_6 (.Clock(Clock), .D(Entrada[5]), .Clear(Clear), .Q(Saida[5]));  // open: nQ
  mips_flipflopD_clear mips_flipflopd_clear_7 (.Clock(Clock), .D(Entrada[6]), .Clear(Clear), .Q(Saida[6]));  // open: nQ
  mips_flipflopD_clear mips_flipflopd_clear_8 (.Clock(Clock), .D(Entrada[7]), .Clear(Clear), .Q(Saida[7]));  // open: nQ
  mips_flipflopD_clear mips_flipflopd_clear_9 (.Clock(Clock), .D(Entrada[8]), .Clear(Clear), .Q(Saida[8]));  // open: nQ
  mips_flipflopD_clear mips_flipflopd_clear_10 (
    .Clock(Clock), .D(Entrada[9]), .Clear(Clear), .Q(Saida[9]));  // open: nQ
  mips_flipflopD_clear mips_flipflopd_clear_11 (
    .Clock(Clock), .D(Entrada[10]), .Clear(Clear), .Q(Saida[10]));  // open: nQ
  mips_flipflopD_clear mips_flipflopd_clear_12 (
    .Clock(Clock), .D(Entrada[11]), .Clear(Clear), .Q(Saida[11]));  // open: nQ
  mips_flipflopD_clear mips_flipflopd_clear_13 (
    .Clock(Clock), .D(Entrada[12]), .Clear(Clear), .Q(Saida[12]));  // open: nQ
  mips_flipflopD_clear mips_flipflopd_clear_14 (
    .Clock(Clock), .D(Entrada[13]), .Clear(Clear), .Q(Saida[13]));  // open: nQ
  mips_flipflopD_clear mips_flipflopd_clear_15 (
    .Clock(Clock), .D(Entrada[14]), .Clear(Clear), .Q(Saida[14]));  // open: nQ
  mips_flipflopD_clear mips_flipflopd_clear_16 (
    .Clock(Clock), .D(Entrada[15]), .Clear(Clear), .Q(Saida[15]));  // open: nQ
  mips_flipflopD_clear mips_flipflopd_clear_17 (
    .Clock(Clock), .D(Entrada[16]), .Clear(Clear), .Q(Saida[16]));  // open: nQ
  mips_flipflopD_clear mips_flipflopd_clear_18 (
    .Clock(Clock), .D(Entrada[17]), .Clear(Clear), .Q(Saida[17]));  // open: nQ
  mips_flipflopD_clear mips_flipflopd_clear_19 (
    .Clock(Clock), .D(Entrada[18]), .Clear(Clear), .Q(Saida[18]));  // open: nQ
  mips_flipflopD_clear mips_flipflopd_clear_20 (
    .Clock(Clock), .D(Entrada[19]), .Clear(Clear), .Q(Saida[19]));  // open: nQ
  mips_flipflopD_clear mips_flipflopd_clear_21 (
    .Clock(Clock), .D(Entrada[20]), .Clear(Clear), .Q(Saida[20]));  // open: nQ
  mips_flipflopD_clear mips_flipflopd_clear_22 (
    .Clock(Clock), .D(Entrada[21]), .Clear(Clear), .Q(Saida[21]));  // open: nQ
  mips_flipflopD_clear mips_flipflopd_clear_23 (
    .Clock(Clock), .D(Entrada[22]), .Clear(Clear), .Q(Saida[22]));  // open: nQ
  mips_flipflopD_clear mips_flipflopd_clear_24 (
    .Clock(Clock), .D(Entrada[23]), .Clear(Clear), .Q(Saida[23]));  // open: nQ
  mips_flipflopD_clear mips_flipflopd_clear_25 (
    .Clock(Clock), .D(Entrada[24]), .Clear(Clear), .Q(Saida[24]));  // open: nQ
  mips_flipflopD_clear mips_flipflopd_clear_26 (
    .Clock(Clock), .D(Entrada[25]), .Clear(Clear), .Q(Saida[25]));  // open: nQ
  mips_flipflopD_clear mips_flipflopd_clear_27 (
    .Clock(Clock), .D(Entrada[26]), .Clear(Clear), .Q(Saida[26]));  // open: nQ
  mips_flipflopD_clear mips_flipflopd_clear_28 (
    .Clock(Clock), .D(Entrada[27]), .Clear(Clear), .Q(Saida[27]));  // open: nQ
  mips_flipflopD_clear mips_flipflopd_clear_29 (
    .Clock(Clock), .D(Entrada[28]), .Clear(Clear), .Q(Saida[28]));  // open: nQ
  mips_flipflopD_clear mips_flipflopd_clear_30 (
    .Clock(Clock), .D(Entrada[29]), .Clear(Clear), .Q(Saida[29]));  // open: nQ
  mips_flipflopD_clear mips_flipflopd_clear_31 (
    .Clock(Clock), .D(Entrada[30]), .Clear(Clear), .Q(Saida[30]));  // open: nQ
  mips_flipflopD_clear mips_flipflopd_clear_32 (
    .Clock(Clock), .D(Entrada[31]), .Clear(Clear), .Q(Saida[31]));  // open: nQ
endmodule
