// Digital circuit mips_ULA1bit_set.dig as structural Verilog
module mips_ULA1bit_set (
  input  Entrada0,
  input  Entrada1,
  input  VemUm,
  input  Less,
  input  Ainvertido,
  input  Binvertido,
  input  [1:0] \Operação ,
  output Resultado,
  output VaiUm,
  output Set
);

  wire and_1_out, mips_mux2_1_p4, mips_mux2_2_p4, not_1_out, not_2_out, or_1_out;

  not not_1 (not_1_out, Entrada0);
  not not_2 (not_2_out, Entrada1);
  // mips_mux2 mips_mux2_1: pin names not known; wires that end beside it: Entrada0, not_1_out, Ainvertido, mips_mux2_1_p4
  // mips_mux2 mips_mux2_2: pin names not known; wires that end beside it: Entrada1, not_2_out, Binvertido, mips_mux2_2_p4
  and and_1 (and_1_out, mips_mux2_1_p4, mips_mux2_2_p4);
  or or_1 (or_1_out, mips_mux2_1_p4, mips_mux2_2_p4);
  mips_somacomplet mips_somacomplet_1 (
    .Entrada0(mips_mux2_1_p4), .Entrada1(mips_mux2_2_p4), .VemUm(VemUm), .Saida(Set), .VaiUm(VaiUm));
  mips_mux4 mips_mux4_1 (
    .Entrada0(and_1_out), .Entrada1(or_1_out), .Entrada2(Set), .Entrada3(Less), .\Seleção0 (\Operação [0]),
    .\Seleção1 (\Operação [1]), .Saida(Resultado));
endmodule

/* Test case:
	Operação	A	B	Ainvert		Binvert		CarryIn		Less	Resultado
loop(a,2)
	loop(b,2)
		0	(a)	(b)	0	0	0	0	(a&b)
		1	(a)	(b)	0	0	0	0	(a|b)
	end loop
end loop
*/
