// Digital circuit mips_ULA32bits.dig as structural Verilog
module mips_ULA32bits (
  input  Binvertido,
  input  Ainvertido,
  input  VemUm,
  input  [1:0] \Operação ,
  input  [31:0] Entrada0,
  input  [31:0] Entrada1,
  output VaiUm,
  output [31:0] Saida
);

  wire mips_ula1bit_set_1_vaium, mips_ula1bit_set_2_vaium, mips_ula1bit_set_3_vaium,
       mips_ula1bit_set_4_vaium, mips_ula1bit_set_5_vaium, mips_ula1bit_set_6_vaium,
       mips_ula1bit_set_7_vaium, mips_ula1bit_set_8_vaium, mips_ula1bit_set_9_vaium,
       mips_ula1bit_set_10_vaium, mips_ula1bit_set_11_vaium, mips_ula1bit_set_12_vaium,
       mips_ula1bit_set_13_vaium, mips_ula1bit_set_14_vaium, mips_ula1bit_set_15_vaium,
       mips_ula1bit_set_16_vaium, mips_ula1bit_set_17_vaium, mips_ula1bit_set_18_vaium,
       mips_ula1bit_set_19_vaium, mips_ula1bit_set_20_vaium, mips_ula1bit_set_21_vaium,
       mips_ula1bit_set_22_vaium, mips_ula1bit_set_23_vaium, mips_ula1bit_set_24_vaium,
       mips_ula1bit_set_25_vaium, mips_ula1bit_set_26_vaium, mips_ula1bit_set_27_vaium,
       mips_ula1bit_set_28_vaium, mips_ula1bit_set_29_vaium, mips_ula1bit_set_30_vaium,
       mips_ula1bit_set_31_vaium, mips_ula1bit_set_32_set;

  mips_ULA1bit_set mips_ula1bit_set_1 (
    .Entrada0(Entrada0[0]), .Entrada1(Entrada1[0]), .VemUm(VemUm), .Less(mips_ula1bit_set_32_set),
    .Ainvertido(Ainvertido), .Binvertido(Binvertido), .\Operação (\Operação ), .Resultado(Saida[0]),
    .VaiUm(mips_ula1bit_set_1_vaium));  // open: Set
  mips_ULA1bit_set mips_ula1bit_set_2 (
    .Entrada0(Entrada0[1]), .Entrada1(Entrada1[1]), .VemUm(mips_ula1bit_set_1_vaium), .Less(1'b0),
    .Ainvertido(Ainvertido), .Binvertido(Binvertido), .\Operação (\Operação ), .Resultado(Saida[1]),
    .VaiUm(mips_ula1bit_set_2_vaium));  // open: Set
  mips_ULA1bit_set mips_ula1bit_set_3 (
    .Entrada0(Entrada0[2]), .Entrada1(Entrada1[2]), .VemUm(mips_ula1bit_set_2_vaium), .Less(1'b0),
    .Ainvertido(Ainvertido), .Binvertido(Binvertido), .\Operação (\Operação ), .Resultado(Saida[2]),
    .VaiUm(mips_ula1bit_set_3_vaium));  // open: Set
  mips_ULA1bit_set mips_ula1bit_set_4 (
    .Entrada0(Entrada0[3]), .Entrada1(Entrada1[3]), .VemUm(mips_ula1bit_set_3_vaium), .Less(1'b0),
    .Ainvertido(Ainvertido), .Binvertido(Binvertido), .\Operação (\Operação ), .Resultado(Saida[3]),
    .VaiUm(mips_ula1bit_set_4_vaium));  // open: Set
  mips_ULA1bit_set mips_ula1bit_set_5 (
    .Entrada0(Entrada0[4]), .Entrada1(Entrada1[4]), .VemUm(mips_ula1bit_set_4_vaium), .Less(1'b0),
    .Ainvertido(Ainvertido), .Binvertido(Binvertido), .\Operação (\Operação ), .Resultado(Saida[4]),
    .VaiUm(mips_ula1bit_set_5_vaium));  // open: Set
  mips_ULA1bit_set mips_ula1bit_set_6 (
    .Entrada0(Entrada0[5]), .Entrada1(Entrada1[5]), .VemUm(mips_ula1bit_set_5_vaium), .Less(1'b0),
    .Ainvertido(Ainvertido), .Binvertido(Binvertido), .\Operação (\Operação ), .Resultado(Saida[5]),
    .VaiUm(mips_ula1bit_set_6_vaium));  // open: Set
  mips_ULA1bit_set mips_ula1bit_set_7 (
    .Entrada0(Entrada0[6]), .Entrada1(Entrada1[6]), .VemUm(mips_ula1bit_set_6_vaium), .Less(1'b0),
    .Ainvertido(Ainvertido), .Binvertido(Binvertido), .\Operação (\Operação ), .Resultado(Saida[6]),
    .VaiUm(mips_ula1bit_set_7_vaium));  // open: Set
  mips_ULA1bit_set mips_ula1bit_set_8 (
    .Entrada0(Entrada0[7]), .Entrada1(Entrada1[7]), .VemUm(mips_ula1bit_set_7_vaium), .Less(1'b0),
    .Ainvertido(Ainvertido), .Binvertido(Binvertido), .\Operação (\Operação ), .Resultado(Saida[7]),
    .VaiUm(mips_ula1bit_set_8_vaium));  // open: Set
  mips_ULA1bit_set mips_ula1bit_set_9 (
    .Entrada0(Entrada0[8]), .Entrada1(Entrada1[8]), .VemUm(mips_ula1bit_set_8_vaium), .Less(1'b0),
    .Ainvertido(Ainvertido), .Binvertido(Binvertido), .\Operação (\Operação ), .Resultado(Saida[8]),
    .VaiUm(mips_ula1bit_set_9_vaium));  // open: Set
  mips_ULA1bit_set mips_ula1bit_set_10 (
    .Entrada0(Entrada0[9]), .Entrada1(Entrada1[9]), .VemUm(mips_ula1bit_set_9_vaium), .Less(1'b0),
    .Ainvertido(Ainvertido), .Binvertido(Binvertido), .\Operação (\Operação ), .Resultado(Saida[9]),
    .VaiUm(mips_ula1bit_set_10_vaium));  // open: Set
  mips_ULA1bit_set mips_ula1bit_set_11 (
    .Entrada0(Entrada0[10]), .Entrada1(Entrada1[10]), .VemUm(mips_ula1bit_set_10_vaium), .Less(1'b0),
    .Ainvertido(Ainvertido), .Binvertido(Binvertido), .\Operação (\Operação ), .Resultado(Saida[10]),
    .VaiUm(mips_ula1bit_set_11_vaium));  // open: Set
  mips_ULA1bit_set mips_ula1bit_set_12 (
    .Entrada0(Entrada0[11]), .Entrada1(Entrada1[11]), .VemUm(mips_ula1bit_set_11_vaium), .Less(1'b0),
    .Ainvertido(Ainvertido), .Binvertido(Binvertido), .\Operação (\Operação ), .Resultado(Saida[11]),
    .VaiUm(mips_ula1bit_set_12_vaium));  // open: Set
  mips_ULA1bit_set mips_ula1bit_set_13 (
    .Entrada0(Entrada0[12]), .Entrada1(Entrada1[12]), .VemUm(mips_ula1bit_set_12_vaium), .Less(1'b0),
    .Ainvertido(Ainvertido), .Binvertido(Binvertido), .\Operação (\Operação ), .Resultado(Saida[12]),
    .VaiUm(mips_ula1bit_set_13_vaium));  // open: Set
  mips_ULA1bit_set mips_ula1bit_set_14 (
    .Entrada0(Entrada0[13]), .Entrada1(Entrada1[13]), .VemUm(mips_ula1bit_set_13_vaium), .Less(1'b0),
    .Ainvertido(Ainvertido), .Binvertido(Binvertido), .\Operação (\Operação ), .Resultado(Saida[13]),
    .VaiUm(mips_ula1bit_set_14_vaium));  // open: Set
  mips_ULA1bit_set mips_ula1bit_set_15 (
    .Entrada0(Entrada0[14]), .Entrada1(Entrada1[14]), .VemUm(mips_ula1bit_set_14_vaium), .Less(1'b0),
    .Ainvertido(Ainvertido), .Binvertido(Binvertido), .\Operação (\Operação ), .Resultado(Saida[14]),
    .VaiUm(mips_ula1bit_set_15_vaium));  // open: Set
  mips_ULA1bit_set mips_ula1bit_set_16 (
    .Entrada0(Entrada0[15]), .Entrada1(Entrada1[15]), .VemUm(mips_ula1bit_set_15_vaium), .Less(1'b0),
    .Ainvertido(Ainvertido), .Binvertido(Binvertido), .\Operação (\Operação ), .Resultado(Saida[15]),
    .VaiUm(mips_ula1bit_set_16_vaium));  // open: Set
  mips_ULA1bit_set mips_ula1bit_set_17 (
    .Entrada0(Entrada0[16]), .Entrada1(Entrada1[16]), .VemUm(mips_ula1bit_set_16_vaium), .Less(1'b0),
    .Ainvertido(Ainvertido), .Binvertido(Binvertido), .\Operação (\Operação ), .Resultado(Saida[16]),
    .VaiUm(mips_ula1bit_set_17_vaium));  // open: Set
  mips_ULA1bit_set mips_ula1bit_set_18 (
    .Entrada0(Entrada0[17]), .Entrada1(Entrada1[17]), .VemUm(mips_ula1bit_set_17_vaium), .Less(1'b0),
    .Ainvertido(Ainvertido), .Binvertido(Binvertido), .\Operação (\Operação ), .Resultado(Saida[17]),
    .VaiUm(mips_ula1bit_set_18_vaium));  // open: Set
  mips_ULA1bit_set mips_ula1bit_set_19 (
    .Entrada0(Entrada0[18]), .Entrada1(Entrada1[18]), .VemUm(mips_ula1bit_set_18_vaium), .Less(1'b0),
    .Ainvertido(Ainvertido), .Binvertido(Binvertido), .\Operação (\Operação ), .Resultado(Saida[18]),
    .VaiUm(mips_ula1bit_set_19_vaium));  // open: Set
  mips_ULA1bit_set mips_ula1bit_set_20 (
    .Entrada0(Entrada0[19]), .Entrada1(Entrada1[19]), .VemUm(mips_ula1bit_set_19_vaium), .Less(1'b0),
    .Ainvertido(Ainvertido), .Binvertido(Binvertido), .\Operação (\Operação ), .Resultado(Saida[19]),
    .VaiUm(mips_ula1bit_set_20_vaium));  // open: Set
  mips_ULA1bit_set mips_ula1bit_set_21 (
    .Entrada0(Entrada0[20]), .Entrada1(Entrada1[20]), .VemUm(mips_ula1bit_set_20_vaium), .Less(1'b0),
    .Ainvertido(Ainvertido), .Binvertido(Binvertido), .\Operação (\Operação ), .Resultado(Saida[20]),
    .VaiUm(mips_ula1bit_set_21_vaium));  // open: Set
  mips_ULA1bit_set mips_ula1bit_set_22 (
    .Entrada0(Entrada0[21]), .Entrada1(Entrada1[21]), .VemUm(mips_ula1bit_set_21_vaium), .Less(1'b0),
    .Ainvertido(Ainvertido), .Binvertido(Binvertido), .\Operação (\Operação ), .Resultado(Saida[21]),
    .VaiUm(mips_ula1bit_set_22_vaium));  // open: Set
  mips_ULA1bit_set mips_ula1bit_set_23 (
    .Entrada0(Entrada0[22]), .Entrada1(Entrada1[22]), .VemUm(mips_ula1bit_set_22_vaium), .Less(1'b0),
    .Ainvertido(Ainvertido), .Binvertido(Binvertido), .\Operação (\Operação ), .Resultado(Saida[22]),
    .VaiUm(mips_ula1bit_set_23_vaium));  // open: Set
  mips_ULA1bit_set mips_ula1bit_set_24 (
    .Entrada0(Entrada0[23]), .Entrada1(Entrada1[23]), .VemUm(mips_ula1bit_set_23_vaium), .Less(1'b0),
    .Ainvertido(Ainvertido), .Binvertido(Binvertido), .\Operação (\Operação ), .Resultado(Saida[23]),
    .VaiUm(mips_ula1bit_set_24_vaium));  // open: Set
  mips_ULA1bit_set mips_ula1bit_set_25 (
    .Entrada0(Entrada0[24]), .Entrada1(Entrada1[24]), .VemUm(mips_ula1bit_set_24_vaium), .Less(1'b0),
    .Ainvertido(Ainvertido), .Binvertido(Binvertido), .\Operação (\Operação ), .Resultado(Saida[24]),
    .VaiUm(mips_ula1bit_set_25_vaium));  // open: Set
  mips_ULA1bit_set mips_ula1bit_set_26 (
    .Entrada0(Entrada0[25]), .Entrada1(Entrada1[25]), .VemUm(mips_ula1bit_set_25_vaium), .Less(1'b0),
    .Ainvertido(Ainvertido), .Binvertido(Binvertido), .\Operação (\Operação ), .Resultado(Saida[25]),
    .VaiUm(mips_ula1bit_set_26_vaium));  // open: Set
  mips_ULA1bit_set mips_ula1bit_set_27 (
    .Entrada0(Entrada0[26]), .Entrada1(Entrada1[26]), .VemUm(mips_ula1bit_set_26_vaium), .Less(1'b0),
    .Ainvertido(Ainvertido), .Binvertido(Binvertido), .\Operação (\Operação ), .Resultado(Saida[26]),
    .VaiUm(mips_ula1bit_set_27_vaium));  // open: Set
  mips_ULA1bit_set mips_ula1bit_set_28 (
    .Entrada0(Entrada0[27]), .Entrada1(Entrada1[27]), .VemUm(mips_ula1bit_set_27_vaium), .Less(1'b0),
    .Ainvertido(Ainvertido), .Binvertido(Binvertido), .\Operação (\Operação ), .Resultado(Saida[27]),
    .VaiUm(mips_ula1bit_set_28_vaium));  // open: Set
  mips_ULA1bit_set mips_ula1bit_set_29 (
    .Entrada0(Entrada0[28]), .Entrada1(Entrada1[28]), .VemUm(mips_ula1bit_set_28_vaium), .Less(1'b0),
    .Ainvertido(Ainvertido), .Binvertido(Binvertido), .\Operação (\Operação ), .Resultado(Saida[28]),
    .VaiUm(mips_ula1bit_set_29_vaium));  // open: Set
  mips_ULA1bit_set mips_ula1bit_set_30 (
    .Entrada0(Entrada0[29]), .Entrada1(Entrada1[29]), .VemUm(mips_ula1bit_set_29_vaium), .Less(1'b0),
    .Ainvertido(Ainvertido), .Binvertido(Binvertido), .\Operação (\Operação ), .Resultado(Saida[29]),
    .VaiUm(mips_ula1bit_set_30_vaium));  // open: Set
  mips_ULA1bit_set mips_ula1bit_set_31 (
    .Entrada0(Entrada0[30]), .Entrada1(Entrada1[30]), .VemUm(mips_ula1bit_set_30_vaium), .Less(1'b0),
    .Ainvertido(Ainvertido), .Binvertido(Binvertido), .\Operação (\Operação ), .Resultado(Saida[30]),
    .VaiUm(mips_ula1bit_set_31_vaium));  // open: Set
  mips_ULA1bit_set mips_ula1bit_set_32 (
    .Entrada0(Entrada0[31]), .Entrada1(Entrada1[31]), .VemUm(mips_ula1bit_set_31_vaium), .Less(1'b0),
    .Ainvertido(Ainvertido), .Binvertido(Binvertido), .\Operação (\Operação ), .Resultado(Saida[31]),
    .VaiUm(VaiUm), .Set(mips_ula1bit_set_32_set));

  // Notes on the sheet:
  //   Less
endmodule

/* Test case:
	Operação	A	B	Ainvert		Binvert		CarryIn		Result31	Result30	Result29	Result28	Result27	Result26	Result25	Result24	Result23	Result22	Result21	Result20	Result19	Result18	Result17	Result16	Result15	Result14	Result13	Result12	Result11	Result10	Result9		Result8		Result7		Result6		Result5		Result4		Result3		Result2		Result1		Result0
loop(a,32)
	loop(b,32)
		0	(a)	(b)	0	0	0	bits(32,a&b)
		1	(a)	(b)	0	0	0	bits(32,a|b)
		10	(a)	(b)	0	0	0	bits(32,a+b)
		10	(a)	(b)	0	1	1	bits(32,a-b)
		0	(a)	(b)	1	1	0	bits(32,~(a|b))
		11	(a)	(b)	0	1	1	bits(32,a-b>31)
	end loop
end loop
*/
