// Digital circuit mips_bancodeReg.dig as structural Verilog
module mips_bancodeReg (
  input  EscreverReg,
  input  [31:0] DadoEscrita__32,
  input  [4:0] RegEscrita__5,
  input  [4:0] RegLeitura1__5,
  input  [4:0] RegLeitura2__5,
  output [31:0] DadoLeitura1,
  output [31:0] DadoLeitura2
);

  wire and_1_out, and_2_out, and_3_out, and_4_out, and_5_out, and_6_out, and_7_out, and_8_out, and_9_out,
       and_10_out, and_11_out, and_12_out, and_13_out, and_14_out, and_15_out, and_16_out, and_17_out,
       and_18_out, and_19_out, and_20_out, and_21_out, and_22_out, and_23_out, and_24_out, and_25_out,
       and_26_out, and_27_out, and_28_out, and_29_out, and_30_out, and_31_out, and_32_out,
       mips_decodificador_1_saida0, mips_decodificador_1_saida1, mips_decodificador_1_saida2,
       mips_decodificador_1_saida3, mips_decodificador_1_saida4, mips_decodificador_1_saida5,
       mips_decodificador_1_saida6, mips_decodificador_1_saida7, mips_decodificador_1_saida8,
       mips_decodificador_1_saida9, mips_decodificador_1_saida10, mips_decodificador_1_saida11,
       mips_decodificador_1_saida12, mips_decodificador_1_saida13, mips_decodificador_1_saida14,
       mips_decodificador_1_saida15, mips_decodificador_1_saida16, mips_decodificador_1_saida17,
       mips_decodificador_1_saida18, mips_decodificador_1_saida19, mips_decodificador_1_saida20,
       mips_decodificador_1_saida21, mips_decodificador_1_saida22, mips_decodificador_1_saida23,
       mips_decodificador_1_saida24, mips_decodificador_1_saida25, mips_decodificador_1_saida26,
       mips_decodificador_1_saida27, mips_decodificador_1_saida28, mips_decodificador_1_saida29,
       mips_decodificador_1_saida30, mips_decodificador_1_saida31;
  wire [31:0] mips_reg32bits_2_p3, mips_reg32bits_3_p3, mips_reg32bits_4_p3, mips_reg32bits_5_p3,
       mips_reg32bits_6_p3, mips_reg32bits_7_p3, mips_reg32bits_8_p3, mips_reg32bits_9_p3,
       mips_reg32bits_10_p3, mips_reg32bits_11_p3, mips_reg32bits_12_p3, mips_reg32bits_13_p3,
       mips_reg32bits_14_p3, mips_reg32bits_15_p3, mips_reg32bits_16_p3, mips_reg32bits_17_p3,
       mips_reg32bits_18_p3, mips_reg32bits_19_p3, mips_reg32bits_20_p3, mips_reg32bits_21_p3,
       mips_reg32bits_22_p3, mips_reg32bits_23_p3, mips_reg32bits_24_p3, mips_reg32bits_25_p3,
       mips_reg32bits_26_p3, mips_reg32bits_27_p3, mips_reg32bits_28_p3, mips_reg32bits_29_p3,
       mips_reg32bits_30_p3, mips_reg32bits_31_p3, mips_reg32bits_32_p3;

  mips_decodificador mips_decodificador_1 (
    .\Endereço (RegEscrita__5), .Saida0(mips_decodificador_1_saida0), .Saida1(mips_decodificador_1_saida1),
    .Saida2(mips_decodificador_1_saida2), .Saida3(mips_decodificador_1_saida3),
    .Saida4(mips_decodificador_1_saida4), .Saida5(mips_decodificador_1_saida5),
    .Saida6(mips_decodificador_1_saida6), .Saida7(mips_decodificador_1_saida7),
    .Saida8(mips_decodificador_1_saida8), .Saida9(mips_decodificador_1_saida9),
    .Saida10(mips_decodificador_1_saida10), .Saida11(mips_decodificador_1_saida11),
    .Saida12(mips_decodificador_1_saida12), .Saida13(mips_decodificador_1_saida13),
    .Saida14(mips_decodificador_1_saida14), .Saida15(mips_decodificador_1_saida15),
    .Saida16(mips_decodificador_1_saida16), .Saida17(mips_decodificador_1_saida17),
    .Saida18(mips_decodificador_1_saida18), .Saida19(mips_decodificador_1_saida19),
    .Saida20(mips_decodificador_1_saida20), .Saida21(mips_decodificador_1_saida21),
    .Saida22(mips_decodificador_1_saida22), .Saida23(mips_decodificador_1_saida23),
    .Saida24(mips_decodificador_1_saida24), .Saida25(mips_decodificador_1_saida25),
    .Saida26(mips_decodificador_1_saida26), .Saida27(mips_decodificador_1_saida27),
    .Saida28(mips_decodificador_1_saida28), .Saida29(mips_decodificador_1_saida29),
    .Saida30(mips_decodificador_1_saida30), .Saida31(mips_decodificador_1_saida31));
  and and_1 (and_1_out, EscreverReg, mips_decodificador_1_saida0);
  and and_2 (and_2_out, EscreverReg, mips_decodificador_1_saida1);
  and and_3 (and_3_out, EscreverReg, mips_decodificador_1_saida2);
  and and_4 (and_4_out, EscreverReg, mips_decodificador_1_saida3);
  and and_5 (and_5_out, EscreverReg, mips_decodificador_1_saida4);
  and and_6 (and_6_out, EscreverReg, mips_decodificador_1_saida5);
  and and_7 (and_7_out, EscreverReg, mips_decodificador_1_saida6);
  and and_8 (and_8_out, EscreverReg, mips_decodificador_1_saida7);
  and and_9 (and_9_out, EscreverReg, mips_decodificador_1_saida8);
  and and_10 (and_10_out, EscreverReg, mips_decodificador_1_saida9);
  and and_11 (and_11_out, EscreverReg, mips_decodificador_1_saida10);
  and and_12 (and_12_out, EscreverReg, mips_decodificador_1_saida11);
  and and_13 (and_13_out, EscreverReg, mips_decodificador_1_saida12);
  and and_14 (and_14_out, EscreverReg, mips_decodificador_1_saida13);
  and and_15 (and_15_out, EscreverReg, mips_decodificador_1_saida14);
  and and_16 (and_16_out, EscreverReg, mips_decodificador_1_saida15);
  and and_17 (and_17_out, EscreverReg, mips_decodificador_1_saida16);
  and and_18 (and_18_out, EscreverReg, mips_decodificador_1_saida17);
  and and_19 (and_19_out, EscreverReg, mips_decodificador_1_saida18);
  and and_20 (and_20_out, EscreverReg, mips_decodificador_1_saida19);
  and and_21 (and_21_out, EscreverReg, mips_decodificador_1_saida20);
  and and_22 (and_22_out, EscreverReg, mips_decodificador_1_saida21);
  and and_23 (and_23_out, EscreverReg, mips_decodificador_1_saida22);
  and and_24 (and_24_out, EscreverReg, mips_decodificador_1_saida23);
  and and_25 (and_25_out, EscreverReg, mips_decodificador_1_saida24);
  and and_26 (and_26_out, EscreverReg, mips_decodificador_1_saida25);
  and and_27 (and_27_out, EscreverReg, mips_decodificador_1_saida26);
  and and_28 (and_28_out, EscreverReg, mips_decodificador_1_saida27);
  and and_29 (and_29_out, EscreverReg, mips_decodificador_1_saida28);
  and and_30 (and_30_out, EscreverReg, mips_decodificador_1_saida29);
  and and_31 (and_31_out, EscreverReg, mips_decodificador_1_saida30);
  and and_32 (and_32_out, EscreverReg, mips_decodificador_1_saida31);
  // mips_reg32bits mips_reg32bits_1: pin names not known; wires that end beside it: DadoEscrita__32, and_1_out
  // mips_reg32bits mips_reg32bits_2: pin names not known; wires that end beside it: DadoEscrita__32, and_2_out, mips_reg32bits_2_p3
  // mips_reg32bits mips_reg32bits_3: pin names not known; wires that end beside it: DadoEscrita__32, and_3_out, mips_reg32bits_3_p3
  // mips_reg32bits mips_reg32bits_4: pin names not known; wires that end beside it: DadoEscrita__32, and_4_out, mips_reg32bits_4_p3
  // mips_reg32bits mips_reg32bits_5: pin names not known; wires that end beside it: DadoEscrita__32, and_5_out, mips_reg32bits_5_p3
  // mips_reg32bits mips_reg32bits_6: pin names not known; wires that end beside it: DadoEscrita__32, and_6_out, mips_reg32bits_6_p3
  // mips_reg32bits mips_reg32bits_7: pin names not known; wires that end beside it: DadoEscrita__32, and_7_out, mips_reg32bits_7_p3
  // mips_reg32bits mips_reg32bits_8: pin names not known; wires that end beside it: DadoEscrita__32, and_8_out, mips_reg32bits_8_p3
  // mips_reg32bits mips_reg32bits_9: pin names not known; wires that end beside it: DadoEscrita__32, and_9_out, mips_reg32bits_9_p3
  // mips_reg32bits mips_reg32bits_10: pin names not known; wires that end beside it: DadoEscrita__32, and_10_out, mips_reg32bits_10_p3
  // mips_reg32bits mips_reg32bits_11: pin names not known; wires that end beside it: DadoEscrita__32, and_11_out, mips_reg32bits_11_p3
  // mips_reg32bits mips_reg32bits_12: pin names not known; wires that end beside it: DadoEscrita__32, and_12_out, mips_reg32bits_12_p3
  // mips_reg32bits mips_reg32bits_13: pin names not known; wires that end beside it: DadoEscrita__32, and_13_out, mips_reg32bits_13_p3
  // mips_reg32bits mips_reg32bits_14: pin names not known; wires that end beside it: DadoEscrita__32, and_14_out, mips_reg32bits_14_p3
  // mips_reg32bits mips_reg32bits_15: pin names not known; wires that end beside it: DadoEscrita__32, and_15_out, mips_reg32bits_15_p3
  // mips_reg32bits mips_reg32bits_16: pin names not known; wires that end beside it: DadoEscrita__32, and_16_out, mips_reg32bits_16_p3
  // mips_reg32bits mips_reg32bits_17: pin names not known; wires that end beside it: DadoEscrita__32, and_17_out, mips_reg32bits_17_p3
  // mips_reg32bits mips_reg32bits_18: pin names not known; wires that end beside it: DadoEscrita__32, and_18_out, mips_reg32bits_18_p3
  // mips_reg32bits mips_reg32bits_19: pin names not known; wires that end beside it: DadoEscrita__32, and_19_out, mips_reg32bits_19_p3
  // mips_reg32bits mips_reg32bits_20: pin names not known; wires that end beside it: DadoEscrita__32, and_20_out, mips_reg32bits_20_p3
  // mips_reg32bits mips_reg32bits_21: pin names not known; wires that end beside it: DadoEscrita__32, and_21_out, mips_reg32bits_21_p3
  // mips_reg32bits mips_reg32bits_22: pin names not known; wires that end beside it: DadoEscrita__32, and_22_out, mips_reg32bits_22_p3
  // mips_reg32bits mips_reg32bits_23: pin names not known; wires that end beside it: DadoEscrita__32, and_23_out, mips_reg32bits_23_p3
  // mips_reg32bits mips_reg32bits_24: pin names not known; wires that end beside it: DadoEscrita__32, and_24_out, mips_reg32bits_24_p3
  // mips_reg32bits mips_reg32bits_25: pin names not known; wires that end beside it: DadoEscrita__32, and_25_out, mips_reg32bits_25_p3
  // mips_reg32bits mips_reg32bits_26: pin names not known; wires that end beside it: DadoEscrita__32, and_26_out, mips_reg32bits_26_p3
  // mips_reg32bits mips_reg32bits_27: pin names not known; wires that end beside it: DadoEscrita__32, and_27_out, mips_reg32bits_27_p3
  // mips_reg32bits mips_reg32bits_28: pin names not known; wires that end beside it: DadoEscrita__32, and_28_out, mips_reg32bits_28_p3
  // mips_reg32bits mips_reg32bits_29: pin names not known; wires that end beside it: DadoEscrita__32, and_29_out, mips_reg32bits_29_p3
  // mips_reg32bits mips_reg32bits_30: pin names not known; wires that end beside it: DadoEscrita__32, and_30_out, mips_reg32bits_30_p3
  // mips_reg32bits mips_reg32bits_31: pin names not known; wires that end beside it: DadoEscrita__32, and_31_out, mips_reg32bits_31_p3
  // mips_reg32bits mips_reg32bits_32: pin names not known; wires that end beside it: DadoEscrita__32, and_32_out, mips_reg32bits_32_p3
  mips_mux32_32bits mips_mux32_32bits_1 (
    .Entrada0({32{1'b0}}), .Entrada1(mips_reg32bits_2_p3), .Entrada2(mips_reg32bits_3_p3),
    .Entrada3(mips_reg32bits_4_p3), .Entrada4(mips_reg32bits_5_p3), .Entrada5(mips_reg32bits_6_p3),
    .Entrada6(mips_reg32bits_7_p3), .Entrada7(mips_reg32bits_8_p3), .Entrada8(mips_reg32bits_9_p3),
    .Entrada9(mips_reg32bits_10_p3), .Entrada10(mips_reg32bits_11_p3), .Entrada11(mips_reg32bits_12_p3),
    .Entrada12(mips_reg32bits_13_p3), .Entrada13(mips_reg32bits_14_p3), .Entrada14(mips_reg32bits_15_p3),
    .Entrada15(mips_reg32bits_16_p3), .Entrada16(mips_reg32bits_17_p3), .Entrada17(mips_reg32bits_18_p3),
    .Entrada18(mips_reg32bits_19_p3), .Entrada19(mips_reg32bits_20_p3), .Entrada20(mips_reg32bits_21_p3),
    .Entrada21(mips_reg32bits_22_p3), .Entrada22(mips_reg32bits_23_p3), .Entrada23(mips_reg32bits_24_p3),
    .Entrada24(mips_reg32bits_25_p3), .Entrada25(mips_reg32bits_26_p3), .Entrada26(mips_reg32bits_27_p3),
    .Entrada27(mips_reg32bits_28_p3), .Entrada28(mips_reg32bits_29_p3), .Entrada29(mips_reg32bits_30_p3),
    .Entrada30(mips_reg32bits_31_p3), .Entrada31(mips_reg32bits_32_p3), .\Seleção (RegLeitura1__5),
    .Saida(DadoLeitura1));
  mips_mux32_32bits mips_mux32_32bits_2 (
    .Entrada0({32{1'b0}}), .Entrada1(mips_reg32bits_2_p3), .Entrada2(mips_reg32bits_3_p3),
    .Entrada3(mips_reg32bits_4_p3), .Entrada4(mips_reg32bits_5_p3), .Entrada5(mips_reg32bits_6_p3),
    .Entrada6(mips_reg32bits_7_p3), .Entrada7(mips_reg32bits_8_p3), .Entrada8(mips_reg32bits_9_p3),
    .Entrada9(mips_reg32bits_10_p3), .Entrada10(mips_reg32bits_11_p3), .Entrada11(mips_reg32bits_12_p3),
    .Entrada12(mips_reg32bits_13_p3), .Entrada13(mips_reg32bits_14_p3), .Entrada14(mips_reg32bits_15_p3),
    .Entrada15(mips_reg32bits_16_p3), .Entrada16(mips_reg32bits_17_p3), .Entrada17(mips_reg32bits_18_p3),
    .Entrada18(mips_reg32bits_19_p3), .Entrada19(mips_reg32bits_20_p3), .Entrada20(mips_reg32bits_21_p3),
    .Entrada21(mips_reg32bits_22_p3), .Entrada22(mips_reg32bits_23_p3), .Entrada23(mips_reg32bits_24_p3),
    .Entrada24(mips_reg32bits_25_p3), .Entrada25(mips_reg32bits_26_p3), .Entrada26(mips_reg32bits_27_p3),
    .Entrada27(mips_reg32bits_28_p3), .Entrada28(mips_reg32bits_29_p3), .Entrada29(mips_reg32bits_30_p3),
    .Entrada30(mips_reg32bits_31_p3), .Entrada31(mips_reg32bits_32_p3), .\Seleção (RegLeitura2__5),
    .Saida(DadoLeitura2));
endmodule
