// Digital circuit mips_decodificador.dig as structural Verilog
module mips_decodificador (
  input  [4:0] \Endereço ,
  output Saida0,
  output Saida1,
  output Saida2,
  output Saida3,
  output Saida4,
  output Saida5,
  output Saida6,
  output Saida7,
  output Saida8,
  output Saida9,
  output Saida10,
  output Saida11,
  output Saida12,
  output Saida13,
  output Saida14,
  output Saida15,
  output Saida16,
  output Saida17,
  output Saida18,
  output Saida19,
  output Saida20,
  output Saida21,
  output Saida22,
  output Saida23,
  output Saida24,
  output Saida25,
  output Saida26,
  output Saida27,
  output Saida28,
  output Saida29,
  output Saida30,
  output Saida31
);

  and and_1 (Saida0, ~\Endereço [4], ~\Endereço [3], ~\Endereço [2], ~\Endereço [1], ~\Endereço [0]);  // And
  and and_2 (Saida1, ~\Endereço [4], ~\Endereço [3], ~\Endereço [2], ~\Endereço [1], \Endereço [0]);  // And
  and and_3 (Saida2, ~\Endereço [4], ~\Endereço [3], ~\Endereço [2], \Endereço [1], ~\Endereço [0]);  // And
  and and_4 (Saida3, ~\Endereço [4], ~\Endereço [3], ~\Endereço [2], \Endereço [1], \Endereço [0]);  // And
  and and_5 (Saida4, ~\Endereço [4], ~\Endereço [3], \Endereço [2], ~\Endereço [1], ~\Endereço [0]);  // And
  and and_6 (Saida5, ~\Endereço [4], ~\Endereço [3], \Endereço [2], ~\Endereço [1], \Endereço [0]);  // And
  and and_7 (Saida6, ~\Endereço [4], ~\Endereço [3], \Endereço [2], \Endereço [1], ~\Endereço [0]);  // And
  and and_8 (Saida7, ~\Endereço [4], ~\Endereço [3], \Endereço [2], \Endereço [1], \Endereço [0]);  // And
  and and_9 (Saida8, ~\Endereço [4], \Endereço [3], ~\Endereço [2], ~\Endereço [1], ~\Endereço [0]);  // And
  and and_10 (Saida9, ~\Endereço [4], \Endereço [3], ~\Endereço [2], ~\Endereço [1], \Endereço [0]);  // And
  and and_11 (Saida10, ~\Endereço [4], \Endereço [3], ~\Endereço [2], \Endereço [1], ~\Endereço [0]);  // And
  and and_12 (Saida11, ~\Endereço [4], \Endereço [3], ~\Endereço [2], \Endereço [1], \Endereço [0]);  // And
  and and_13 (Saida12, ~\Endereço [4], \Endereço [3], \Endereço [2], ~\Endereço [1], ~\Endereço [0]);  // And
  and and_14 (Saida13, ~\Endereço [4], \Endereço [3], \Endereço [2], ~\Endereço [1], \Endereço [0]);  // And
  and and_15 (Saida14, ~\Endereço [4], \Endereço [3], \Endereço [2], \Endereço [1], ~\Endereço [0]);  // And
  and and_16 (Saida15, ~\Endereço [4], \Endereço [3], \Endereço [2], \Endereço [1], \Endereço [0]);  // And
  and and_17 (Saida16, \Endereço [4], ~\Endereço [3], ~\Endereço [2], ~\Endereço [1], ~\Endereço [0]);  // And
  and and_18 (Saida17, \Endereço [4], ~\Endereço [3], ~\Endereço [2], ~\Endereço [1], \Endereço [0]);  // And
  and and_19 (Saida18, \Endereço [4], ~\Endereço [3], ~\Endereço [2], \Endereço [1], ~\Endereço [0]);  // And
  and and_20 (Saida19, \Endereço [4], ~\Endereço [3], ~\Endereço [2], \Endereço [1], \Endereço [0]);  // And
  and and_21 (Saida20, \Endereço [4], ~\Endereço [3], \Endereço [2], ~\Endereço [1], ~\Endereço [0]);  // And
  and and_22 (Saida21, \Endereço [4], ~\Endereço [3], \Endereço [2], ~\Endereço [1], \Endereço [0]);  // And
  and and_23 (Saida22, \Endereço [4], ~\Endereço [3], \Endereço [2], \Endereço [1], ~\Endereço [0]);  // And
  and and_24 (Saida23, \Endereço [4], ~\Endereço [3], \Endereço [2], \Endereço [1], \Endereço [0]);  // And
  and and_25 (Saida24, \Endereço [4], \Endereço [3], ~\Endereço [2], ~\Endereço [1], ~\Endereço [0]);  // And
  and and_26 (Saida25, \Endereço [4], \Endereço [3], ~\Endereço [2], ~\Endereço [1], \Endereço [0]);  // And
  and and_27 (Saida26, \Endereço [4], \Endereço [3], ~\Endereço [2], \Endereço [1], ~\Endereço [0]);  // And
  and and_28 (Saida27, \Endereço [4], \Endereço [3], ~\Endereço [2], \Endereço [1], \Endereço [0]);  // And
  and and_29 (Saida28, \Endereço [4], \Endereço [3], \Endereço [2], ~\Endereço [1], ~\Endereço [0]);  // And
  and and_30 (Saida29, \Endereço [4], \Endereço [3], \Endereço [2], ~\Endereço [1], \Endereço [0]);  // And
  and and_31 (Saida30, \Endereço [4], \Endereço [3], \Endereço [2], \Endereço [1], ~\Endereço [0]);  // And
  and and_32 (Saida31, \Endereço [4], \Endereço [3], \Endereço [2], \Endereço [1], \Endereço [0]);
endmodule
