// Digital circuit mips_flipflopD.dig as structural Verilog
module mips_flipflopD (
  input  Clock,
  input  D,
  output Q,
  output nQ
);

  wire mips_latchd_1_p3, not_1_out;

  // mips_latchD mips_latchd_1: pin names not known; wires that end beside it: Clock, D, mips_latchd_1_p3
  not not_1 (not_1_out, Clock);
  // mips_latchD mips_latchd_2: pin names not known; wires that end beside it: not_1_out, mips_latchd_1_p3, Q, nQ

  // Notes on the sheet:
  //   Borda de descida
endmodule
