// Digital circuit mips_flipflopD_clear.dig as structural Verilog
module mips_flipflopD_clear (
  input  Clock,
  input  D,
  input  Clear,
  output Q,
  output nQ
);

  wire mips_latchd_clear_1_q, not_1_out;

  mips_latchD_clear mips_latchd_clear_1 (.Clock(Clock), .D(D), .Clear(Clear), .Q(mips_latchd_clear_1_q));  // open: nQ
  not not_1 (not_1_out, Clock);
  mips_latchD_clear mips_latchd_clear_2 (.Clock(not_1_out), .D(mips_latchd_clear_1_q), .Clear(Clear), .Q(Q), .nQ(nQ));
endmodule
