// Digital circuit mips_latchD_clear.dig as structural Verilog
module mips_latchD_clear (
  input  Clock,
  input  D,
  input  Clear,
  output Q,
  output nQ
);

  wire and_1_out, and_2_out;

  and and_1 (and_1_out, Clock, ~D);  // And
  and and_2 (and_2_out, Clock, D);
  nor nor_1 (Q, and_1_out, Clear, nQ);
  nor nor_2 (nQ, Q, and_2_out);
endmodule
