// Digital circuit mips_memoria_instrução.dig as structural Verilog
module \mips_memoria_instrução  (
  input  [31:0] \Endereço__32 ,
  output [31:0] \Instrução 
);

  ROM #(.AddrBits(24), .Bits(32), .Addr_Bits(15)) rom_1 (.A(\Endereço__32 [25:2]), .sel(1'b1), .D(\Instrução ));

  // Notes on the sheet:
  //   Instrução: bidirectional data bus
  //   {{de Der bidirektionelle Datenbus}}
  //   Endereço__32: address bus
  //   {{de Der Adressbus}}
  //   *Usamos o distribuidor porque o 
  //   endereçamento do MIPS é por byte 
  //   e a ROM do Digital é por palavra. 
  //   E assim usamos palavra de 32 
  //   bits.
  //   *Os bits 26-31 é pela limitação do 
  //   tamanho máximo da memória que é 
  //   possível simular no Digital.
  //   contents of rom_1 (hex, n*v repeats v):
  //   20080005,2108000a
  //   *O valor fixo em 1 é porque essa 
  //   memória foi projetada para 
  //   trabalhar com múltiplos bancos 
  //   de memória e usamos apenas 
  //   uma.
endmodule
