// Digital circuit mips_mux2_32bits.dig as structural Verilog
module mips_mux2_32bits (
  input  [31:0] Entrada0,
  input  [31:0] Entrada1,
  input  \Seleção ,
  output [31:0] \Saída 
);

  // mips_mux2 mips_mux2_1: pin names not known; wires that end beside it: Entrada0[0], Entrada1[0], \Seleção , \Saída [0]
  // mips_mux2 mips_mux2_2: pin names not known; wires that end beside it: Entrada0[1], Entrada1[1], \Seleção , \Saída [1]
  // mips_mux2 mips_mux2_3: pin names not known; wires that end beside it: Entrada0[2], Entrada1[2], \Seleção , \Saída [2]
  // mips_mux2 mips_mux2_4: pin names not known; wires that end beside it: Entrada0[3], Entrada1[3], \Seleção , \Saída [3]
  // mips_mux2 mips_mux2_5: pin names not known; wires that end beside it: Entrada0[4], Entrada1[4], \Seleção , \Saída [4]
  // mips_mux2 mips_mux2_6: pin names not known; wires that end beside it: Entrada0[5], Entrada1[5], \Seleção , \Saída [5]
  // mips_mux2 mips_mux2_7: pin names not known; wires that end beside it: Entrada0[6], Entrada1[6], \Seleção , \Saída [6]
  // mips_mux2 mips_mux2_8: pin names not known; wires that end beside it: Entrada0[7], Entrada1[7], \Seleção , \Saída [7]
  // mips_mux2 mips_mux2_9: pin names not known; wires that end beside it: Entrada0[8], Entrada1[8], \Seleção , \Saída [8]
  // mips_mux2 mips_mux2_10: pin names not known; wires that end beside it: Entrada0[9], Entrada1[9], \Seleção , \Saída [9]
  // mips_mux2 mips_mux2_11: pin names not known; wires that end beside it: Entrada0[10], Entrada1[10], \Seleção , \Saída [10]
  // mips_mux2 mips_mux2_12: pin names not known; wires that end beside it: Entrada0[11], Entrada1[11], \Seleção , \Saída [11]
  // mips_mux2 mips_mux2_13: pin names not known; wires that end beside it: Entrada0[12], Entrada1[12], \Seleção , \Saída [12]
  // mips_mux2 mips_mux2_14: pin names not known; wires that end beside it: Entrada0[13], Entrada1[13], \Seleção , \Saída [13]
  // mips_mux2 mips_mux2_15: pin names not known; wires that end beside it: Entrada0[14], Entrada1[14], \Seleção , \Saída [14]
  // mips_mux2 mips_mux2_16: pin names not known; wires that end beside it: Entrada0[15], Entrada1[15], \Seleção , \Saída [15]
  // mips_mux2 mips_mux2_17: pin names not known; wires that end beside it: Entrada0[16], Entrada1[16], \Seleção , \Saída [16]
  // mips_mux2 mips_mux2_18: pin names not known; wires that end beside it: Entrada0[17], Entrada1[17], \Seleção , \Saída [17]
  // mips_mux2 mips_mux2_19: pin names not known; wires that end beside it: Entrada0[18], Entrada1[18], \Seleção , \Saída [18]
  // mips_mux2 mips_mux2_20: pin names not known; wires that end beside it: Entrada0[19], Entrada1[19], \Seleção , \Saída [19]
  // mips_mux2 mips_mux2_21: pin names not known; wires that end beside it: Entrada0[20], Entrada1[20], \Seleção , \Saída [20]
  // mips_mux2 mips_mux2_22: pin names not known; wires that end beside it: Entrada0[21], Entrada1[21], \Seleção , \Saída [21]
  // mips_mux2 mips_mux2_23: pin names not known; wires that end beside it: Entrada0[22], Entrada1[22], \Seleção , \Saída [22]
  // mips_mux2 mips_mux2_24: pin names not known; wires that end beside it: Entrada0[23], Entrada1[23], \Seleção , \Saída [23]
  // mips_mux2 mips_mux2_25: pin names not known; wires that end beside it: Entrada0[24], Entrada1[24], \Seleção , \Saída [24]
  // mips_mux2 mips_mux2_26: pin names not known; wires that end beside it: Entrada0[25], Entrada1[25], \Seleção , \Saída [25]
  // mips_mux2 mips_mux2_27: pin names not known; wires that end beside it: Entrada0[26], Entrada1[26], \Seleção , \Saída [26]
  // mips_mux2 mips_mux2_28: pin names not known; wires that end beside it: Entrada0[27], Entrada1[27], \Seleção , \Saída [27]
  // mips_mux2 mips_mux2_29: pin names not known; wires that end beside it: Entrada0[28], Entrada1[28], \Seleção , \Saída [28]
  // mips_mux2 mips_mux2_30: pin names not known; wires that end beside it: Entrada0[29], Entrada1[29], \Seleção , \Saída [29]
  // mips_mux2 mips_mux2_31: pin names not known; wires that end beside it: Entrada0[30], Entrada1[30], \Seleção , \Saída [30]
  // mips_mux2 mips_mux2_32: pin names not known; wires that end beside it: Entrada0[31], Entrada1[31], \Seleção , \Saída [31]
endmodule
