// Digital circuit mips_mux32_32bits.dig as structural Verilog
module mips_mux32_32bits (
  input  [31:0] Entrada0,
  input  [31:0] Entrada1,
  input  [31:0] Entrada2,
  input  [31:0] Entrada3,
  input  [31:0] Entrada4,
  input  [31:0] Entrada5,
  input  [31:0] Entrada6,
  input  [31:0] Entrada7,
  input  [31:0] Entrada8,
  input  [31:0] Entrada9,
  input  [31:0] Entrada10,
  input  [31:0] Entrada11,
  input  [31:0] Entrada12,
  input  [31:0] Entrada13,
  input  [31:0] Entrada14,
  input  [31:0] Entrada15,
  input  [31:0] Entrada16,
  input  [31:0] Entrada17,
  input  [31:0] Entrada18,
  input  [31:0] Entrada19,
  input  [31:0] Entrada20,
  input  [31:0] Entrada21,
  input  [31:0] Entrada22,
  input  [31:0] Entrada23,
  input  [31:0] Entrada24,
  input  [31:0] Entrada25,
  input  [31:0] Entrada26,
  input  [31:0] Entrada27,
  input  [31:0] Entrada28,
  input  [31:0] Entrada29,
  input  [31:0] Entrada30,
  input  [31:0] Entrada31,
  input  [4:0] \Seleção ,
  output [31:0] Saida
);

  wire [31:0] mips_mux16_32bits_1_saida, mips_mux16_32bits_2_saida;

  mips_mux16_32bits mips_mux16_32bits_1 (
    .Entrada0(Entrada0), .Entrada1(Entrada1), .Entrada2(Entrada2), .Entrada3(Entrada3), .Entrada4(Entrada4),
    .Entrada5(Entrada5), .Entrada6(Entrada6), .Entrada7(Entrada7), .Entrada8(Entrada8), .Entrada9(Entrada9),
    .Entrada10(Entrada10), .Entrada11(Entrada11), .Entrada12(Entrada12), .Entrada13(Entrada13),
    .Entrada14(Entrada14), .Entrada15(Entrada15), .S0(\Seleção [0]), .S1(\Seleção [1]), .S2(\Seleção [2]),
    .S3(\Seleção [3]), .Saida(mips_mux16_32bits_1_saida));
  mips_mux16_32bits mips_mux16_32bits_2 (
    .Entrada0(Entrada16), .Entrada1(Entrada17), .Entrada2(Entrada18), .Entrada3(Entrada19),
    .Entrada4(Entrada20), .Entrada5(Entrada21), .Entrada6(Entrada22), .Entrada7(Entrada23),
    .Entrada8(Entrada24), .Entrada9(Entrada25), .Entrada10(Entrada26), .Entrada11(Entrada27),
    .Entrada12(Entrada28), .Entrada13(Entrada29), .Entrada14(Entrada30), .Entrada15(Entrada31),
    .S0(\Seleção [0]), .S1(\Seleção [1]), .S2(\Seleção [2]), .S3(\Seleção [3]),
    .Saida(mips_mux16_32bits_2_saida));
  mips_mux2_32bits mips_mux2_32bits_1 (
    .Entrada0(mips_mux16_32bits_1_saida), .Entrada1(mips_mux16_32bits_2_saida), .\Seleção (\Seleção [4]),
    .\Saída (Saida));
endmodule
