// Digital circuit mips_mux4.dig as structural Verilog
module mips_mux4 (
  input  Entrada0,
  input  Entrada1,
  input  Entrada2,
  input  Entrada3,
  input  \Seleção0 ,
  input  \Seleção1 ,
  output Saida
);

  wire and_1_out, and_2_out, and_3_out, and_4_out, not_1_out, not_2_out;

  not not_1 (not_1_out, \Seleção0 );
  not not_2 (not_2_out, \Seleção1 );
  and and_1 (and_1_out, Entrada0, not_2_out, not_1_out);
  and and_2 (and_2_out, Entrada1, \Seleção0 , not_2_out);
  and and_3 (and_3_out, Entrada2, \Seleção1 , not_1_out);
  and and_4 (and_4_out, Entrada3, \Seleção0 , \Seleção1 );
  or or_1 (Saida, and_1_out, and_2_out, and_3_out, and_4_out);
endmodule
