// Digital circuit mips_somacomplet.dig as structural Verilog
module mips_somacomplet (
  input  Entrada0,
  input  Entrada1,
  input  VemUm,
  output Saida,
  output VaiUm
);

  wire and_1_out, and_2_out, xor_1_out;

  xor xor_1 (xor_1_out, Entrada0, Entrada1);
  and and_1 (and_1_out, Entrada0, Entrada1);
  xor xor_2 (Saida, VemUm, xor_1_out);
  and and_2 (and_2_out, xor_1_out, VemUm);
  or or_1 (VaiUm, and_2_out, and_1_out);
endmodule
