// Digital circuit mips_somador32bits.dig as structural Verilog
module mips_somador32bits (
  input  [31:0] A,
  input  [31:0] B,
  input  Cin,
  output Cout,
  output [31:0] \Saída 
);

  wire mips_somacomplet_1_vaium, mips_somacomplet_2_vaium, mips_somacomplet_3_vaium,
       mips_somacomplet_4_vaium, mips_somacomplet_5_vaium, mips_somacomplet_6_vaium,
       mips_somacomplet_7_vaium, mips_somacomplet_8_vaium, mips_somacomplet_9_vaium,
       mips_somacomplet_10_vaium, mips_somacomplet_11_vaium, mips_somacomplet_12_vaium,
       mips_somacomplet_13_vaium, mips_somacomplet_14_vaium, mips_somacomplet_15_vaium,
       mips_somacomplet_16_vaium, mips_somacomplet_17_vaium, mips_somacomplet_18_vaium,
       mips_somacomplet_19_vaium, mips_somacomplet_20_vaium, mips_somacomplet_21_vaium,
       mips_somacomplet_22_vaium, mips_somacomplet_23_vaium, mips_somacomplet_24_vaium,
       mips_somacomplet_25_vaium, mips_somacomplet_26_vaium, mips_somacomplet_27_vaium,
       mips_somacomplet_28_vaium, mips_somacomplet_29_vaium, mips_somacomplet_30_vaium,
       mips_somacomplet_31_vaium;

  mips_somacomplet mips_somacomplet_1 (
    .Entrada0(A[0]), .Entrada1(B[0]), .VemUm(Cin), .Saida(\Saída [0]), .VaiUm(mips_somacomplet_1_vaium));
  mips_somacomplet mips_somacomplet_2 (
    .Entrada0(A[1]), .Entrada1(B[1]), .VemUm(mips_somacomplet_1_vaium), .Saida(\Saída [1]),
    .VaiUm(mips_somacomplet_2_vaium));
  mips_somacomplet mips_somacomplet_3 (
    .Entrada0(A[2]), .Entrada1(B[2]), .VemUm(mips_somacomplet_2_vaium), .Saida(\Saída [2]),
    .VaiUm(mips_somacomplet_3_vaium));
  mips_somacomplet mips_somacomplet_4 (
    .Entrada0(A[3]), .Entrada1(B[3]), .VemUm(mips_somacomplet_3_vaium), .Saida(\Saída [3]),
    .VaiUm(mips_somacomplet_4_vaium));
  mips_somacomplet mips_somacomplet_5 (
    .Entrada0(A[4]), .Entrada1(B[4]), .VemUm(mips_somacomplet_4_vaium), .Saida(\Saída [4]),
    .VaiUm(mips_somacomplet_5_vaium));
  mips_somacomplet mips_somacomplet_6 (
    .Entrada0(A[5]), .Entrada1(B[5]), .VemUm(mips_somacomplet_5_vaium), .Saida(\Saída [5]),
    .VaiUm(mips_somacomplet_6_vaium));
  mips_somacomplet mips_somacomplet_7 (
    .Entrada0(A[6]), .Entrada1(B[6]), .VemUm(mips_somacomplet_6_vaium), .Saida(\Saída [6]),
    .VaiUm(mips_somacomplet_7_vaium));
  mips_somacomplet mips_somacomplet_8 (
    .Entrada0(A[7]), .Entrada1(B[7]), .VemUm(mips_somacomplet_7_vaium), .Saida(\Saída [7]),
    .VaiUm(mips_somacomplet_8_vaium));
  mips_somacomplet mips_somacomplet_9 (
    .Entrada0(A[8]), .Entrada1(B[8]), .VemUm(mips_somacomplet_8_vaium), .Saida(\Saída [8]),
    .VaiUm(mips_somacomplet_9_vaium));
  mips_somacomplet mips_somacomplet_10 (
    .Entrada0(A[9]), .Entrada1(B[9]), .VemUm(mips_somacomplet_9_vaium), .Saida(\Saída [9]),
    .VaiUm(mips_somacomplet_10_vaium));
  mips_somacomplet mips_somacomplet_11 (
    .Entrada0(A[10]), .Entrada1(B[10]), .VemUm(mips_somacomplet_10_vaium), .Saida(\Saída [10]),
    .VaiUm(mips_somacomplet_11_vaium));
  mips_somacomplet mips_somacomplet_12 (
    .Entrada0(A[11]), .Entrada1(B[11]), .VemUm(mips_somacomplet_11_vaium), .Saida(\Saída [11]),
    .VaiUm(mips_somacomplet_12_vaium));
  mips_somacomplet mips_somacomplet_13 (
    .Entrada0(A[12]), .Entrada1(B[12]), .VemUm(mips_somacomplet_12_vaium), .Saida(\Saída [12]),
    .VaiUm(mips_somacomplet_13_vaium));
  mips_somacomplet mips_somacomplet_14 (
    .Entrada0(A[13]), .Entrada1(B[13]), .VemUm(mips_somacomplet_13_vaium), .Saida(\Saída [13]),
    .VaiUm(mips_somacomplet_14_vaium));
  mips_somacomplet mips_somacomplet_15 (
    .Entrada0(A[14]), .Entrada1(B[14]), .VemUm(mips_somacomplet_14_vaium), .Saida(\Saída [14]),
    .VaiUm(mips_somacomplet_15_vaium));
  mips_somacomplet mips_somacomplet_16 (
    .Entrada0(A[15]), .Entrada1(B[15]), .VemUm(mips_somacomplet_15_vaium), .Saida(\Saída [15]),
    .VaiUm(mips_somacomplet_16_vaium));
  mips_somacomplet mips_somacomplet_17 (
    .Entrada0(A[16]), .Entrada1(B[16]), .VemUm(mips_somacomplet_16_vaium), .Saida(\Saída [16]),
    .VaiUm(mips_somacomplet_17_vaium));
  mips_somacomplet mips_somacomplet_18 (
    .Entrada0(A[17]), .Entrada1(B[17]), .VemUm(mips_somacomplet_17_vaium), .Saida(\Saída [17]),
    .VaiUm(mips_somacomplet_18_vaium));
  mips_somacomplet mips_somacomplet_19 (
    .Entrada0(A[18]), .Entrada1(B[18]), .VemUm(mips_somacomplet_18_vaium), .Saida(\Saída [18]),
    .VaiUm(mips_somacomplet_19_vaium));
  mips_somacomplet mips_somacomplet_20 (
    .Entrada0(A[19]), .Entrada1(B[19]), .VemUm(mips_somacomplet_19_vaium), .Saida(\Saída [19]),
    .VaiUm(mips_somacomplet_20_vaium));
  mips_somacomplet mips_somacomplet_21 (
    .Entrada0(A[20]), .Entrada1(B[20]), .VemUm(mips_somacomplet_20_vaium), .Saida(\Saída [20]),
    .VaiUm(mips_somacomplet_21_vaium));
  mips_somacomplet mips_somacomplet_22 (
    .Entrada0(A[21]), .Entrada1(B[21]), .VemUm(mips_somacomplet_21_vaium), .Saida(\Saída [21]),
    .VaiUm(mips_somacomplet_22_vaium));
  mips_somacomplet mips_somacomplet_23 (
    .Entrada0(A[22]), .Entrada1(B[22]), .VemUm(mips_somacomplet_22_vaium), .Saida(\Saída [22]),
    .VaiUm(mips_somacomplet_23_vaium));
  mips_somacomplet mips_somacomplet_24 (
    .Entrada0(A[23]), .Entrada1(B[23]), .VemUm(mips_somacomplet_23_vaium), .Saida(\Saída [23]),
    .VaiUm(mips_somacomplet_24_vaium));
  mips_somacomplet mips_somacomplet_25 (
    .Entrada0(A[24]), .Entrada1(B[24]), .VemUm(mips_somacomplet_24_vaium), .Saida(\Saída [24]),
    .VaiUm(mips_somacomplet_25_vaium));
  mips_somacomplet mips_somacomplet_26 (
    .Entrada0(A[25]), .Entrada1(B[25]), .VemUm(mips_somacomplet_25_vaium), .Saida(\Saída [25]),
    .VaiUm(mips_somacomplet_26_vaium));
  mips_somacomplet mips_somacomplet_27 (
    .Entrada0(A[26]), .Entrada1(B[26]), .VemUm(mips_somacomplet_26_vaium), .Saida(\Saída [26]),
    .VaiUm(mips_somacomplet_27_vaium));
  mips_somacomplet mips_somacomplet_28 (
    .Entrada0(A[27]), .Entrada1(B[27]), .VemUm(mips_somacomplet_27_vaium), .Saida(\Saída [27]),
    .VaiUm(mips_somacomplet_28_vaium));
  mips_somacomplet mips_somacomplet_29 (
    .Entrada0(A[28]), .Entrada1(B[28]), .VemUm(mips_somacomplet_28_vaium), .Saida(\Saída [28]),
    .VaiUm(mips_somacomplet_29_vaium));
  mips_somacomplet mips_somacomplet_30 (
    .Entrada0(A[29]), .Entrada1(B[29]), .VemUm(mips_somacomplet_29_vaium), .Saida(\Saída [29]),
    .VaiUm(mips_somacomplet_30_vaium));
  mips_somacomplet mips_somacomplet_31 (
    .Entrada0(A[30]), .Entrada1(B[30]), .VemUm(mips_somacomplet_30_vaium), .Saida(\Saída [30]),
    .VaiUm(mips_somacomplet_31_vaium));
  mips_somacomplet mips_somacomplet_32 (
    .Entrada0(A[31]), .Entrada1(B[31]), .VemUm(mips_somacomplet_31_vaium), .Saida(\Saída [31]), .VaiUm(Cout));
endmodule
