// Digital circuit mips_testando_instrucao_ADDI.dig as structural Verilog
module mips_testando_instrucao_ADDI (
  input  [31:0] Escreve_Dado,
  input  Escrever,
  input  [1:0] in_4,
  input  Clock,
  input  Clear,
  output [31:0] Saida
);

  wire [4:0] \mips_memoria_instrução_1_instrução_2 , \mips_memoria_instrução_1_instrução_3 ;
  wire [31:0] mips_bancodereg_1_dadoleitura1, mips_bancodereg_1_dadoleitura2,
       \mips_memoria_instrução_1_instrução , mips_pc_4_1_saida;

  mips_PC_4 mips_pc_4_1 (.Clock(Clock), .Clear(Clear), .Saida(mips_pc_4_1_saida));
  \mips_memoria_instrução  \mips_memoria_instrução_1  (
    .\Instrução ({\mips_memoria_instrução_1_instrução [31:26], \mips_memoria_instrução_1_instrução_3 , \mips_memoria_instrução_1_instrução_2 , \mips_memoria_instrução_1_instrução [15:0]}),
    .\Endereço__32 (mips_pc_4_1_saida));
  mips_bancodeReg mips_bancodereg_1 (
    .EscreverReg(Escrever), .DadoEscrita__32(Escreve_Dado),
    .RegEscrita__5(\mips_memoria_instrução_1_instrução_2 ),
    .RegLeitura1__5(\mips_memoria_instrução_1_instrução_3 ),
    .RegLeitura2__5(\mips_memoria_instrução_1_instrução_2 ), .DadoLeitura1(mips_bancodereg_1_dadoleitura1),
    .DadoLeitura2(mips_bancodereg_1_dadoleitura2));
  mips_ULA32bits mips_ula32bits_1 (
    .Binvertido(1'b0), .Ainvertido(1'b0), .VemUm(1'b0), .\Operação (in_4),
    .Entrada0(mips_bancodereg_1_dadoleitura1), .Entrada1(mips_bancodereg_1_dadoleitura2), .Saida(Saida));  // open: VaiUm
endmodule
